# Fritzing sketch NovoPainel (saved by Fritzing 0.9.2b)
circuit board: 19cm x 5.64444cm
breadboards: 1

parts:
  J3 = female pin header, 2 pins [form="♀ (female)"]
  C2 = Electrolytic Capacitor [capacitance=100µF package="200 mil [THT, electrolytic]"]
  U1 = Voltage Regulator [package=to220-adj]
  C3 = Electrolytic Capacitor [capacitance=100µF package="200 mil [THT, electrolytic]"]
  J5 = female pin header, 2 pins [form="♀ (female)"]
  J6 = Screw terminal - 2 pins [package=THT]
  J7 = Screw terminal - 2 pins [package=THT]
  J8 = female pin header, 2 pins [form="♀ (female)"]
  J9 = female pin header, 2 pins [form="♀ (female)"]
  J10 = Screw terminal - 2 pins [package=THT]
  C4 = Electrolytic Capacitor [capacitance=100µF package="200 mil [THT, electrolytic]"]
  R3 = Resistor [tolerance=±5% resistance=220 package=THT]
  J12 = female pin header, 2 pins [form="♀ (female)"]
  D1 = Diode [package=diode-hv]
  D2 = Diode [package=diode-hv]
  J13 = female pin header, 2 pins [form="♀ (female)"]
  R4 = Resistor [tolerance=±5% resistance=220 package=THT]
  C5 = Electrolytic Capacitor [capacitance=100µF package="200 mil [THT, electrolytic]"]
  J15 = female pin header, 2 pins [form="♀ (female)"]
  R1 = Resistor [tolerance=±5% resistance=220 package=THT]
  U2 = POT [package=3362u]
  J14 = female pin header, 2 pins [form="♀ (female)"]

nets:
  N1: J3.pin1, C2.+, U1.IN, J8.pin1, J9.pin2, J13.pin2
  N2: J3.pin2, C2.-, C3.-, J5.pin2, J6.pin1, J7.pin1, J10.pin1, C4.-, J12.pin1, C5.-, J15.pin1, U2.E, J14.pin1
  N3: U1.ADJ, R1.Pin_1, U2.S, U2.A
  N4: U1.OUT, C3.+, J5.pin1, R1.Pin_0
  N5: J6.pin2, D1.A
  N6: J7.pin2, D2.A
  N7: J8.pin2, D1.C, D2.C
  N8: J9.pin1, J10.pin2, C4.+, R3.Pin_0
  N9: R3.Pin_1, J12.pin2
  N10: J13.pin1, R4.Pin_0, C5.+, J15.pin2
  N11: R4.Pin_1, J14.pin2

notes:
  +
  -
  B1
  B2
  V1
  S1
  Baterias em paralelo
  Switch geral do robo
  voltímetro
  switch dos motores
  saída dos motores
  regulador ajustável
  Aqui comeca a alimentacao dos outros componentes
  Voltimetro
  LED
  switch do arduino
  saída do arduino
